// Logisim project Fibonacci_Sequence_Generator_Circuit.circ as structural Verilog: 1 circuit, main circuit main
module main (
  input  set_num2
);

  wire button_1_out, clock_1_out;
  wire [7:0] adder_1_out, num1_q, num2_q;

  Clock clock_1 (.out(clock_1_out));
  Button button_1 (.out(button_1_out));
  Register num1 (.D(num2_q), .clk(clock_1_out), .Q(num1_q), .clr(button_1_out));  // open: en
  Adder adder_1 (.a(num1_q), .b(num2_q), .out(adder_1_out), .cin(set_num2));  // open: cout
  Register num2 (.D(adder_1_out), .clk(clock_1_out), .Q(num2_q), .clr(button_1_out));  // open: en
  LED led_1 (.in(adder_1_out[4]));
  LED led_2 (.in(adder_1_out[6]));
  LED led_3 (.in(adder_1_out[5]));
  LED led_4 (.in(adder_1_out[7]));
  LED led_5 (.in(adder_1_out[2]));
  LED led_6 (.in(adder_1_out[1]));
  LED led_7 (.in(adder_1_out[3]));
  LED led_8 (.in(adder_1_out[0]));

  // Notes on the sheet:
  //   clock
  //   reset
  //   Fibonacci Sequence Generator Logic Circuit
  //   64
  //   32
  //   16
  //   128
  //   fib_out
  //   4
  //   1
  //   2
  //   8
endmodule
