# Fritzing sketch Star_Trek_Clock_Schematic (saved by Fritzing 0.9.7b)
breadboards: 1

parts:
  Part1 = Arduino Nano (Rev3.0)
  DFRobot_DFPlayer_Mini1 = DFRobot DFPlayer Mini [part_number=DFR0299]
  J1 = Power Jack [package=power_jack_slot]
  SP1 = SPEAKER [package=pcb_mount_speaker]
  R1 = Resistor [tolerance=±5% resistance=1k package="1206 [SMD]"]
  LED1 = smd LED [color="Red (633nm)" package="0805 [SMD]"]
  LED2 = smd LED [color="Red (633nm)" package="0805 [SMD]"]
  LED3 = smd LED [color="Red (633nm)" package="0805 [SMD]"]
  LED4 = smd LED [color="Red (633nm)" package="0805 [SMD]"]
  LED5 = smd LED [color="Blue (470nm)" package="0805 [SMD]"]
  LED6 = smd LED [color="Blue (470nm)" package="0805 [SMD]"]
  LED7 = smd LED [color="Blue (470nm)" package="0805 [SMD]"]
  LED8 = smd LED [color="Blue (470nm)" package="0805 [SMD]"]
  LED9 = smd LED [color="Blue (470nm)" package="0805 [SMD]"]
  LED10 = smd LED [color="Blue (470nm)" package="0805 [SMD]"]
  LED11 = smd LED [color="White (6500K)" package="0805 [SMD]"]
  LED12 = smd LED [color="White (6500K)" package="0805 [SMD]"]
  S1 = Pushbutton [package="[THT]"]
  S2 = Pushbutton [package="[THT]"]
  R2 = Resistor [tolerance=±5% resistance=330 package="0402 [SMD]"]
  R3 = Resistor [tolerance=±5% resistance=330 package="0402 [SMD]"]
  R4 = Resistor [tolerance=±5% resistance=330 package="0402 [SMD]"]
  R5 = Resistor [tolerance=±5% resistance=330 package="0402 [SMD]"]
  R6 = Resistor [tolerance=±5% resistance=330 package="0402 [SMD]"]
  R7 = Resistor [tolerance=±5% resistance=330 package="0402 [SMD]"]
  R8 = Resistor [tolerance=±5% resistance=330 package="0402 [SMD]"]
  R9 = Resistor [tolerance=±5% resistance=330 package="0402 [SMD]"]
  R10 = Resistor [tolerance=±5% resistance=330 package="0402 [SMD]"]
  R11 = Resistor [tolerance=±5% resistance=330 package="0402 [SMD]"]
  R12 = Resistor [tolerance=±5% resistance=330 package="0402 [SMD]"]

nets:
  N1: Part1.GND, DFRobot_DFPlayer_Mini1.GND-1, DFRobot_DFPlayer_Mini1.GND-2, S1.Pin_3, S2.Pin_1, S2.Pin_2
  N2: Part1.D2, LED10.cathode, LED10.anode, R7.Pin_0
  N3: Part1.D3, LED9.anode, R6.Pin_0
  N4: Part1.D4, LED7.cathode, LED7.anode, R4.Pin_0
  N5: Part1.D5, LED8.cathode, LED8.anode
  N6: Part1.D6, LED5.cathode, LED5.anode, R2.Pin_0
  N7: Part1.D7, LED6.cathode, LED6.anode, R3.Pin_0
  N8: Part1.D8, DFRobot_DFPlayer_Mini1.TX
  N9: Part1.D9, LED4.anode
  N10: Part1.D10, LED3.cathode, LED3.anode
  N11: Part1.D11/MOSI, LED2.cathode, LED2.anode
  N12: Part1.D12/MISO, LED1.anode, R12.Pin_0
  VIN: Part1.VIN, DFRobot_DFPlayer_Mini1.VCC, J1.PWR
  N13: Part1.A2, LED11.anode, LED12.anode
  N14: Part1.A1, S2.Pin_3
  N15: Part1.A0, S1.Pin_1
  N16: Part1.D13/SCK, R1.Pin_0
  N17: DFRobot_DFPlayer_Mini1.RX, R1.Pin_1
  N18: DFRobot_DFPlayer_Mini1.SPK_2, SP1.+
  N19: LED11.cathode, LED12.cathode, R8.Pin_0
  N20: R2.Pin_1, R3.Pin_1, R4.Pin_1, R5.Pin_1, R6.Pin_1, R7.Pin_1, R8.Pin_1, R9.Pin_1, R10.Pin_1, R11.Pin_1, R12.Pin_1
